# Fritzing sketch Projeto Alarme - Esquema (saved by Fritzing 0.9.3b)
breadboards: 1

parts:
  Componente1 = Arduino Uno (Rev3)
  U5 = RELAY [package=relay-jzc]  # not connected
  Sensore_PIR_HC-SR502 = HC-SR501 Body Sensor Module
  Sensore_PIR_HC-SR503 = HC-SR501 Body Sensor Module  # not connected
  S4 = Magnetic Door Switch [package=reed_switch_plastic]  # not connected
  J1 = Piezo Speaker
  W5500_Module2 = W5500 Ethernet module [package="DIP (Dual Inline) [THT]"]

nets:
  N1: Componente1.D8, Sensore_PIR_HC-SR502.OUT
  N2: Componente1.D10_PWM/SS, W5500_Module2.SCS
  N3: Componente1.D11_PWM/MOSI, W5500_Module2.MOSI
  N4: Componente1.D12/MISO, W5500_Module2.MISO
  N5: Componente1.D13/SCK, W5500_Module2.SCLK
  N6: Componente1.D2, W5500_Module2.INT
  N7: Componente1.D7, J1.pin2
  3V3: Componente1.3V3, W5500_Module2.3.3V
  5V: Componente1.5V, Sensore_PIR_HC-SR502.VCC
  GND: Componente1.GND, Sensore_PIR_HC-SR502.GND, J1.pin1

notes:
  - GND
  + 5v
  Buzina
  Relê 12v, NA
  Pendente:
  * ligação SIM800
  * Buzzer
  * Relê

custom parts:
  HC-SR501 Body Sensor Module: Pyroelectric Infrared PIR Motion Sensor Detector Module
  W5500 Ethernet module: W5500 based SPI Ethernet module for Arduino, etc.
